# Fritzing sketch SoilMoistureCheckerOled (saved by Fritzing 0.9.4)
breadboards: 1

parts:
  Squix2 = OLED 0.96" 128x64 I2C SSD1306 (GND/VCC)
  U2 = NodeMCU V1.0
  Componente1 = Soil Moisture Sensor

nets:
  GND: Squix2.GND, U2.GND, Componente1.GND
  VCC: Squix2.VCC, U2.3V3, Componente1.VCC
  N1: Squix2.SCL, U2.D1
  N2: Squix2.SCA, U2.D2
  N3: U2.A0, Componente1.SIG

custom parts:
  OLED 0.96" 128x64 I2C SSD1306 (GND/VCC): OLED 0.96" 128x64 I2C SSD1306 Pinout: GND/VCC/SCL/SDA
  NodeMCU V1.0: ESP8266 based NodeMCU
